# Fritzing sketch simpleShiftRegister (saved by Fritzing 0.9.2b)
breadboards: 1

parts:
  U1 = 74HC595 SMD [package="SO16 [SMD]"]
  Composant1 = Arduino Due (Rev2b)
  R1 = Resistor [tolerance=±5% resistance=330 package=THT]
  LED1 = LED - 5mm [color="Red (633nm)" package="5 mm [THT]"]
  LED2 = LED - 5mm [color="Red (633nm)" package="5 mm [THT]"]
  LED3 = LED - 5mm [color="Red (633nm)" package="5 mm [THT]"]
  LED4 = LED - 5mm [color="Red (633nm)" package="5 mm [THT]"]
  LED5 = LED - 5mm [color="Red (633nm)" package="5 mm [THT]"]
  LED6 = LED - 5mm [color="Red (633nm)" package="5 mm [THT]"]
  LED7 = LED - 5mm [color="Red (633nm)" package="5 mm [THT]"]
  LED8 = LED - 5mm [color="Red (633nm)" package="5 mm [THT]"]
  R2 = Resistor [tolerance=±5% resistance=330 package=THT]
  R3 = Resistor [tolerance=±5% resistance=330 package=THT]
  R4 = Resistor [tolerance=±5% resistance=330 package=THT]
  R5 = Resistor [tolerance=±5% resistance=330 package=THT]
  R6 = Resistor [tolerance=±5% resistance=330 package=THT]
  R7 = Resistor [tolerance=±5% resistance=330 package=THT]
  R8 = Resistor [tolerance=±5% resistance=330 package=THT]

nets:
  N1: U1.Q1, R2.Pin_1
  N2: U1.Q2, R3.Pin_1
  N3: U1.Q3, R4.Pin_1
  N4: U1.Q4, R5.Pin_1
  N5: U1.Q5, R7.Pin_1
  N6: U1.Q6, R6.Pin_1
  N7: U1.Q7, R8.Pin_1
  GND: U1.GND, U1.OE, Composant1.GND, LED1.anode, LED2.anode, LED3.anode, LED4.anode, LED5.anode, LED6.anode, LED7.anode, LED8.anode
  VCC: U1.MR, U1.VCC, Composant1.5V
  N8: U1.SH_CP, Composant1.D13_PWM
  N9: U1.ST_CP, Composant1.D10_PWM/SS0
  N10: U1.DS, Composant1.D11_PWM
  N11: U1.Q0, R1.Pin_1
  N12: R1.Pin_0, LED1.cathode
  N13: LED2.cathode, R2.Pin_0
  N14: LED3.cathode, R3.Pin_0
  N15: LED4.cathode, R4.Pin_0
  N16: LED5.cathode, R7.Pin_0
  N17: LED6.cathode, R5.Pin_0
  N18: LED7.cathode, R8.Pin_0
  N19: LED8.cathode, R6.Pin_0
